# Fritzing sketch DetectorMovimentoDistancia (saved by Fritzing 0.8.7b)
breadboards: 1

parts:
  Componente1 = Arduino Uno (Rev3)
  LED1 = LED - 5mm [color="Blue (430nm)" package="5 mm [THT]"]
  LED2 = LED - 5mm [color="Red (633nm)" package="5 mm [THT]"]
  J1 = Piezo Speaker
  R1 = Resistor [tolerance=±5% resistance=1k package=THT]
  R3 = Resistor [tolerance=±5% resistance=1k package=THT]
  PIR1 = PIR sensor
  Componente2 = SRF05 Ultrasonic Rangefinder

nets:
  N1: Componente1.D8, LED2.cathode
  N2: Componente1.D9_PWM, LED1.cathode
  N3: Componente1.D10_PWM/SS, Componente2.Echo
  N4: Componente1.D11_PWM/MOSI, Componente2.Trig
  N5: Componente1.D2, PIR1.SIG
  N6: Componente1.D3_PWM, J1.pin2
  5V: Componente1.5V, PIR1.VDD, Componente2.VCC
  GND: Componente1.GND, J1.pin1, R1.Pin_1, R3.Pin_1, PIR1.GND, Componente2.GND
  N7: LED1.anode, R3.Pin_0
  N8: LED2.anode, R1.Pin_0
